// Logisim project HW5_RBN_2306173113_AthazahraNabilaRuby.circ as structural Verilog: 4 circuits, main circuit FullAdder
module FullAdder (
  input  Cin,
  input  A,
  input  B,
  output S,
  output Cout
);

  wire and_1_out, and_2_out, and_3_out, xor_1_out;

  xor xor_1 (xor_1_out, B, A);
  and and_1 (and_1_out, B, A);
  and and_2 (and_2_out, B, Cin);
  and and_3 (and_3_out, A, Cin);
  xor xor_2 (S, xor_1_out, Cin);
  // OR_Gate or_1: pin names not known; wires that end beside it: and_1_out, and_2_out, and_3_out, Cout
endmodule

module Adder_Subtractor (
  input  B3,
  input  A3,
  input  B2,
  input  A2,
  input  B1,
  input  A1,
  input  B0,
  input  A0,
  input  S,
  output S3,
  output S2,
  output S1,
  output S0,
  output Overflow
);

  wire fulladder_1_cout, fulladder_2_cout, fulladder_3_cout, fulladder_4_cout, xor_1_out, xor_3_out,
       xor_4_out, xor_5_out;

  xor xor_1 (xor_1_out, B3, S);
  FullAdder fulladder_1 (.Cin(fulladder_2_cout), .A(A3), .B(xor_1_out), .S(S3), .Cout(fulladder_1_cout));
  xor xor_2 (Overflow, fulladder_1_cout, fulladder_2_cout);
  xor xor_3 (xor_3_out, B2, S);
  FullAdder fulladder_2 (.Cin(fulladder_3_cout), .A(A2), .B(xor_3_out), .S(S2), .Cout(fulladder_2_cout));
  xor xor_4 (xor_4_out, B1, S);
  FullAdder fulladder_3 (.Cin(fulladder_4_cout), .A(A1), .B(xor_4_out), .S(S1), .Cout(fulladder_3_cout));
  xor xor_5 (xor_5_out, B0, S);
  FullAdder fulladder_4 (.Cin(S), .A(A0), .B(xor_5_out), .S(S0), .Cout(fulladder_4_cout));
endmodule

module TwosToOnes (
  input  A3,
  input  A2,
  input  A1,
  input  A0,
  output S3,
  output S2,
  output S1,
  output S0,
  output Overflow
);

  wire fulladder_1_cout, fulladder_2_cout, fulladder_3_cout, fulladder_4_cout, xor_1_out, xor_3_out,
       xor_4_out, xor_5_out;

  xor xor_1 (xor_1_out, 1'b0, 1'b1);
  FullAdder fulladder_1 (.Cin(fulladder_2_cout), .A(A3), .B(xor_1_out), .S(S3), .Cout(fulladder_1_cout));
  xor xor_2 (Overflow, fulladder_1_cout, fulladder_2_cout);
  xor xor_3 (xor_3_out, 1'b0, 1'b1);
  FullAdder fulladder_2 (.Cin(fulladder_3_cout), .A(A2), .B(xor_3_out), .S(S2), .Cout(fulladder_2_cout));
  xor xor_4 (xor_4_out, 1'b0, 1'b1);
  FullAdder fulladder_3 (.Cin(fulladder_4_cout), .A(A1), .B(xor_4_out), .S(S1), .Cout(fulladder_3_cout));
  xor xor_5 (xor_5_out, 1'b1, 1'b1);
  FullAdder fulladder_4 (.Cin(1'b1), .A(A0), .B(xor_5_out), .S(S0), .Cout(fulladder_4_cout));
endmodule

module MainCircuit (
  input  [3:0] A,
  input  [3:0] B,
  input  S,
  output O_2S,
  output O_1S,
  output [3:0] F
);

  wire adder_subtractor_1_s0, adder_subtractor_1_s1, adder_subtractor_1_s2, adder_subtractor_1_s3;

  Adder_Subtractor adder_subtractor_1 (
    .B3(B[3]), .A3(A[3]), .B2(B[2]), .A2(A[2]), .B1(B[1]), .A1(A[1]), .B0(B[0]), .A0(A[0]), .S(S),
    .S3(adder_subtractor_1_s3), .S2(adder_subtractor_1_s2), .S1(adder_subtractor_1_s1),
    .S0(adder_subtractor_1_s0), .Overflow(O_2S));
  TwosToOnes twostoones_1 (
    .A3(adder_subtractor_1_s3), .A2(adder_subtractor_1_s2), .A1(adder_subtractor_1_s1),
    .A0(adder_subtractor_1_s0), .S3(F[3]), .S2(F[2]), .S1(F[1]), .S0(F[0]), .Overflow(O_1S));

  // Notes on the sheet:
  //   Overflow? (2s)
  //   Overflow? (1s)
endmodule
