// Logisim project HW6_RBN_2306173113_AthazahraNabilaRuby.circ as structural Verilog: 4 circuits, main circuit Combinational_3
module Combinational_3 (
  input  A,
  input  B,
  input  C,
  input  X,
  output D2,
  output D1,
  output D0,
  output Y
);

  wire and_1_out, and_2_out, and_3_out, and_4_out, and_5_out, and_6_out, and_7_out, not_1_out, not_2_out,
       not_3_out, not_4_out, or_1_out, or_2_out;

  not not_1 (not_1_out, A);
  not not_2 (not_2_out, B);
  not not_3 (not_3_out, C);
  not not_4 (not_4_out, X);
  or or_1 (or_1_out, not_4_out, C, A);
  or or_2 (or_2_out, not_3_out, not_1_out);
  and and_1 (and_1_out, or_1_out, B);
  and and_2 (and_2_out, not_4_out, C, A);
  and and_3 (and_3_out, X, not_3_out, not_2_out, not_1_out);
  and and_4 (and_4_out, or_2_out, not_4_out);
  and and_5 (and_5_out, not_3_out, B, not_1_out);
  and and_6 (and_6_out, not_4_out, C, B);
  and and_7 (and_7_out, X, not_3_out, not_2_out, A);
  or or_3 (D2, and_1_out, and_2_out, and_3_out);
  or or_4 (D0, and_4_out, and_5_out);
  or or_5 (Y, and_6_out, and_7_out);

  assign D1 = X;

  // Notes on the sheet:
  //   Combinational Circuit for No. 3
endmodule

module Sequential_3 (
  input  X,
  output Y
);

  wire clock_1_out, combinational_3_1_d0, combinational_3_1_d1, combinational_3_1_d2, D0_q, D1_q, D2_q;

  Clock clock_1 (.out(clock_1_out));
  Combinational_3 combinational_3_1 (
    .A(D2_q), .B(D1_q), .C(D0_q), .X(X), .D2(combinational_3_1_d2), .D1(combinational_3_1_d1),
    .D0(combinational_3_1_d0), .Y(Y));
  D_Flip_Flop D2 (.D(combinational_3_1_d2), .clk(clock_1_out), .Q(D2_q));  // open: Qn, preset, reset
  D_Flip_Flop D1 (.D(combinational_3_1_d1), .clk(clock_1_out), .Q(D1_q));  // open: Qn, preset, reset
  D_Flip_Flop D0 (.D(combinational_3_1_d0), .clk(clock_1_out), .Q(D0_q));  // open: Qn, preset, reset

  // Notes on the sheet:
  //   Sequential Circuit for No. 3
endmodule

module Combinational_4 (
  input  A,
  input  B,
  input  C,
  input  X,
  output JA,
  output KA,
  output JB,
  output KB,
  output JC,
  output KC,
  output Y
);

  not not_1 (KC, X);
  and and_1 (JA, KC, C, B);
  and and_2 (JB, KC, C);
  or or_1 (KB, KC, C);

  assign JC = X;
  assign KA = JA;
  assign Y = A;

  // Notes on the sheet:
  //   Combinational Circuit for No. 4
endmodule

module Sequential_4 (
  input  X,
  output Y
);

  wire clock_1_out, combinational_4_1_ja, combinational_4_1_jb, combinational_4_1_jc, combinational_4_1_ka,
       combinational_4_1_kb, combinational_4_1_kc, JKA_q, JKB_q, JKC_q;

  Clock clock_1 (.out(clock_1_out));
  Combinational_4 combinational_4_1 (
    .A(JKA_q), .B(JKB_q), .C(JKC_q), .X(X), .JA(combinational_4_1_ja), .KA(combinational_4_1_ka),
    .JB(combinational_4_1_jb), .KB(combinational_4_1_kb), .JC(combinational_4_1_jc),
    .KC(combinational_4_1_kc), .Y(Y));
  J_K_Flip_Flop JKA (
    .J(combinational_4_1_ja), .K(combinational_4_1_ka), .clk(clock_1_out), .Q(JKA_q));  // open: Qn, preset, reset
  J_K_Flip_Flop JKB (
    .J(combinational_4_1_jb), .K(combinational_4_1_kb), .clk(clock_1_out), .Q(JKB_q));  // open: Qn, preset, reset
  J_K_Flip_Flop JKC (
    .J(combinational_4_1_jc), .K(combinational_4_1_kc), .clk(clock_1_out), .Q(JKC_q));  // open: Qn, preset, reset

  // Notes on the sheet:
  //   Sequential Circuit for No. 4
endmodule
