// Logisim project HW8_RBN_2306173113_AthazahraNabilaRuby.circ as structural Verilog: 1 circuit, main circuit main
module main (
  input  E
);

  wire and_1_out, and_2_out, and_3_out, clock_1_out, not_1_out, or_1_out, S0_q, S0_qn, S1_q, S1_qn, xor_1_out;

  not not_1 (not_1_out, E);
  and and_1 (and_1_out, not_1_out, S1_q);
  and and_2 (and_2_out, E, S0_qn, S1_qn);
  and and_3 (and_3_out, S0_q, S1_q);
  or or_1 (or_1_out, and_1_out, and_2_out, and_3_out);
  xor xor_1 (xor_1_out, S0_q, E);
  D_Flip_Flop S1 (.D(or_1_out), .clk(clock_1_out), .Q(S1_q), .Qn(S1_qn));  // open: preset, reset
  D_Flip_Flop S0 (.D(xor_1_out), .clk(clock_1_out), .Q(S0_q), .Qn(S0_qn));  // open: preset, reset
  Clock clock_1 (.out(clock_1_out));
endmodule
