// Logisim project LAB2_RBN_2306173113_AthazahraNabilaRuby.circ as structural Verilog: 2 circuits, main circuit SOP
module SOP (
  input  A,
  input  B,
  input  C,
  input  D,
  output O
);

  wire and_1_out, and_2_out, not_1_out, not_2_out, not_3_out;

  not not_1 (not_1_out, A);
  not not_2 (not_2_out, C);
  not not_3 (not_3_out, D);
  and and_1 (and_1_out, C, B, A);
  and and_2 (and_2_out, not_2_out, B, not_1_out);
  or or_1 (O, and_1_out, not_3_out, and_2_out);

  // Notes on the sheet:
  //   SUM OF PRODUCT (SOP)
endmodule

module POS (
  input  A,
  input  B,
  input  C,
  input  D,
  output O
);

  wire not_1_out, not_2_out, not_3_out, or_1_out, or_2_out, or_3_out, or_4_out;

  not not_1 (not_1_out, A);
  not not_2 (not_2_out, C);
  not not_3 (not_3_out, D);
  or or_1 (or_1_out, not_3_out, B, not_1_out);
  or or_2 (or_2_out, not_3_out, C, not_1_out);
  or or_3 (or_3_out, not_3_out, B, A);
  or or_4 (or_4_out, not_3_out, not_2_out, A);
  and and_1 (O, or_1_out, or_2_out, or_3_out, or_4_out);

  // Notes on the sheet:
  //   PRODUCT OF SUMTERMS (POS)
endmodule
