// Logisim project LAB3_RBN_2306173113_AthazahraNabilaRuby.circ as structural Verilog: 1 circuit, main circuit Code_Converter
module Code_Converter (
  input  A,
  input  B,
  input  C,
  input  D,
  output W,
  output X,
  output Y,
  output Z
);

  wire nor_1_out, nor_2_out, nor_4_out, nor_5_out, nor_6_out, nor_7_out, nor_8_out, nor_9_out, nor_10_out;

  nor nor_1 (nor_1_out, B, B);
  nor nor_2 (nor_2_out, C, C);
  nor nor_3 (Z, D, D);
  nor nor_4 (nor_4_out, C, B, A);
  nor nor_5 (nor_5_out, D, B, A);
  nor nor_6 (nor_6_out, C, nor_1_out);
  nor nor_7 (nor_7_out, D, nor_1_out);
  nor nor_8 (nor_8_out, Z, nor_2_out, B);
  nor nor_9 (nor_9_out, D, C);
  nor nor_10 (nor_10_out, Z, nor_2_out);
  nor nor_11 (W, nor_4_out, nor_5_out);
  nor nor_12 (X, nor_6_out, nor_7_out, nor_8_out);
  nor nor_13 (Y, nor_9_out, nor_10_out);

  // Notes on the sheet:
  //   LAB 3 - Athazahra Nabila Ruby
  //   B'
  //   C'
  //   D'
  //   (A+B+C)'
  //   (A+B+D)'
  //   (B'+C)'
  //   (B'+D)'
  //   (B+C'+D')'
  //   (C+D)'
  //   (C'+D')'
endmodule
