// Logisim project LAB4_RBN_2306173113_AthazahraNabilaRuby.circ as structural Verilog: 7 circuits, main circuit ParAdder
module main (
  input  [3:0] X,
  input  [3:0] Y,
  input  [1:0] A,
  output [3:0] R
);

  wire [3:0] onecomp_1_y, paradder_1_s, paradder_2_s;

  ParAdder paradder_1 (.X(X), .Y(Y), .Z(1'b0), .S(paradder_1_s));
  OneComp onecomp_1 (.X(X), .Y(onecomp_1_y));
  ParAdder paradder_2 (.X(onecomp_1_y), .Y(4'b0001), .Z(1'b0), .S(paradder_2_s));
  FourOneMul fouronemul_1 (.D0(paradder_1_s), .D1(onecomp_1_y), .D2(paradder_2_s), .A(A), .R(R));

  // Notes on the sheet:
  //   X + Y
  //   1's Complement Converter
  //   What about 2's Complement?
endmodule

module FullAdder (
  input  X,
  input  Y,
  input  Z,
  output S,
  output C
);

  wire and_1_out, and_2_out, and_3_out, xor_1_out;

  xor xor_1 (xor_1_out, Z, Y);
  and and_1 (and_1_out, Y, X);
  and and_2 (and_2_out, Z, Y);
  and and_3 (and_3_out, Z, X);
  xor xor_2 (S, xor_1_out, X);
  or or_1 (C, and_1_out, and_2_out, and_3_out);

  // Notes on the sheet:
  //   1. Full Adder
  //   XY
  //   YZ
  //   XZ
endmodule

module ParAdder (
  input  [3:0] X,
  input  [3:0] Y,
  input  Z,
  output [3:0] S
);

  wire fulladder_1_c, fulladder_2_c, fulladder_3_c;

  FullAdder fulladder_1 (.X(X[0]), .Y(Y[0]), .Z(Z), .S(S[0]), .C(fulladder_1_c));
  FullAdder fulladder_2 (.X(X[1]), .Y(Y[1]), .Z(fulladder_1_c), .S(S[1]), .C(fulladder_2_c));
  FullAdder fulladder_3 (.X(X[2]), .Y(Y[2]), .Z(fulladder_2_c), .S(S[2]), .C(fulladder_3_c));
  FullAdder fulladder_4 (.X(X[3]), .Y(Y[3]), .Z(fulladder_3_c), .S(S[3]));  // open: C

  // Notes on the sheet:
  //   Parallel Adder
endmodule

module OneComp (
  input  [3:0] X,
  output [3:0] Y
);

  not not_1 (Y[0], X[0]);
  not not_2 (Y[1], X[1]);
  not not_3 (Y[2], X[2]);
  not not_4 (Y[3], X[3]);
endmodule

module TwoFourDec (
  input  A0,
  input  A1,
  output D0,
  output D1,
  output D2,
  output D3
);

  wire not_1_out, not_2_out;

  not not_1 (not_1_out, A0);
  not not_2 (not_2_out, A1);
  and and_1 (D0, not_2_out, not_1_out);
  and and_2 (D1, not_2_out, A0);
  and and_3 (D2, A1, not_1_out);
  and and_4 (D3, A1, A0);

  // Notes on the sheet:
  //   2-To-4 Decoder
endmodule

module FourOneMul (
  input  [3:0] D0,
  input  [3:0] D1,
  input  [3:0] D2,
  input  [1:0] A,
  output [3:0] R
);

  wire twofourdec_1_d0, twofourdec_1_d1, twofourdec_1_d2;
  wire [3:0] and_1_out, and_2_out, and_3_out, bit_extender_1_out, bit_extender_2_out, bit_extender_3_out;

  TwoFourDec twofourdec_1 (
    .A0(A[0]), .A1(A[1]), .D0(twofourdec_1_d0), .D1(twofourdec_1_d1), .D2(twofourdec_1_d2));  // open: D3
  assign bit_extender_1_out = {{3{twofourdec_1_d0}}, twofourdec_1_d0};  // Bit_Extender bit_extender_1
  assign bit_extender_2_out = {{3{twofourdec_1_d1}}, twofourdec_1_d1};  // Bit_Extender bit_extender_2
  assign bit_extender_3_out = {{3{twofourdec_1_d2}}, twofourdec_1_d2};  // Bit_Extender bit_extender_3
  assign and_1_out = bit_extender_1_out & D0;  // AND_Gate and_1, 4 bits wide
  assign and_2_out = bit_extender_2_out & D1;  // AND_Gate and_2, 4 bits wide
  assign and_3_out = bit_extender_3_out & D2;  // AND_Gate and_3, 4 bits wide
  assign R = and_1_out | and_2_out | and_3_out;  // OR_Gate or_1, 4 bits wide

  // Notes on the sheet:
  //   4-Bit 4-to-1 Multiplexer
  //   Don't make any changes to this circuit!
  //   Bit extender from 1 bit to 4 bits
endmodule

module ya (
  input  A,
  input  B,
  input  C,
  output F
);

  wire nand_1_out, nand_2_out, nand_3_out, not_1_out, not_2_out;

  not not_1 (not_1_out, A);
  not not_2 (not_2_out, C);
  nand nand_1 (nand_1_out, not_1_out, B, not_2_out);
  nand nand_2 (nand_2_out, A, B, not_2_out);
  nand nand_3 (nand_3_out, A, B, C);
  nand nand_4 (F, nand_1_out, nand_2_out, nand_3_out);
endmodule
