// Logisim project LAB6_RBN_2306173113_AthazahraNabilaRuby.circ as structural Verilog: 2 circuits, main circuit Combinatorial
module Combinatorial (
  input  X,
  input  Y,
  input  Z,
  input  A,
  input  B,
  output T,
  output J,
  output K,
  output D,
  output O
);

  wire and_1_out, and_2_out, not_1_out, not_2_out, or_1_out, or_2_out, xnor_1_out;

  not not_1 (not_1_out, X);
  not not_2 (not_2_out, B);
  or or_1 (or_1_out, B, A, Z);
  or or_2 (or_2_out, A, Z);
  and and_1 (and_1_out, or_1_out, X);
  and and_2 (and_2_out, or_2_out, not_2_out, Y);
  xnor xnor_1 (xnor_1_out, A, Z);
  or or_3 (T, and_1_out, and_2_out);
  and and_3 (J, or_2_out, not_2_out, not_1_out);
  or or_4 (K, B, A, Z);
  and and_4 (D, xnor_1_out, not_2_out);
  and and_5 (O, or_2_out, not_2_out, X);
endmodule

module Sequential (
  input  A,
  input  B,
  output O
);

  wire clock_1_out, combinatorial_1_d, combinatorial_1_j, combinatorial_1_k, combinatorial_1_t, FX_q, FY_q,
       FZ_q;

  Clock clock_1 (.out(clock_1_out));
  Combinatorial combinatorial_1 (
    .X(FX_q), .Y(FY_q), .Z(FZ_q), .A(A), .B(B), .T(combinatorial_1_t), .J(combinatorial_1_j),
    .K(combinatorial_1_k), .D(combinatorial_1_d), .O(O));
  T_Flip_Flop FX (.T(combinatorial_1_t), .clk(clock_1_out), .Q(FX_q));  // open: Qn, reset, preset
  J_K_Flip_Flop FY (
    .J(combinatorial_1_j), .K(combinatorial_1_k), .clk(clock_1_out), .Q(FY_q));  // open: Qn, preset, reset
  D_Flip_Flop FZ (.D(combinatorial_1_d), .clk(clock_1_out), .Q(FZ_q));  // open: Qn, preset, reset
endmodule
