// Logisim project LAB7_RBN_2306173113_AthazahraNabilaRuby.circ as structural Verilog: 4 circuits, main circuit Combinational
module Combinational (
  input  At,
  input  B,
  input  S0,
  input  S1,
  output At1
);

  wire and_1_out, and_2_out, and_3_out, not_1_out, not_2_out, or_1_out, xor_1_out;

  not not_1 (not_1_out, S0);
  not not_2 (not_2_out, At);
  or or_1 (or_1_out, B, S1);
  xor xor_1 (xor_1_out, At, S0);
  and and_1 (and_1_out, or_1_out, xor_1_out);
  and and_2 (and_2_out, ~or_1_out, not_2_out, not_1_out);  // AND_Gate
  and and_3 (and_3_out, B, not_1_out, S1);
  or or_2 (At1, and_1_out, and_2_out, and_3_out);
endmodule

module CombinationalWithMux (
  input  At,
  input  B,
  input  S0,
  input  S1,
  output At1
);

  wire and_1_out, not_1_out, not_2_out, or_1_out, xor_1_out;

  not not_1 (not_1_out, At);
  not not_2 (not_2_out, B);
  xor xor_1 (xor_1_out, not_2_out, At);
  and and_1 (and_1_out, B, not_1_out);
  or or_1 (or_1_out, B, At);
  Multiplexer #(.select(2)) multiplexer_1 (
    .in0(xor_1_out), .in1(and_1_out), .in2(or_1_out), .in3(not_1_out), .out(At1), .sel({S1, S0}));
endmodule

module WithoutMux (
  input  S1,
  input  S0,
  input  [3:0] B,
  input  Reset,
  output [3:0] At1
);

  wire Clk_out, combinational_1_at1, combinational_2_at1, combinational_3_at1, combinational_4_at1;

  Combinational combinational_1 (.At(At1[0]), .B(B[0]), .S0(S0), .S1(S1), .At1(combinational_1_at1));
  Combinational combinational_2 (.At(At1[1]), .B(B[1]), .S0(S0), .S1(S1), .At1(combinational_2_at1));
  Combinational combinational_3 (.At(At1[2]), .B(B[2]), .S0(S0), .S1(S1), .At1(combinational_3_at1));
  Combinational combinational_4 (.At(At1[3]), .B(B[3]), .S0(S0), .S1(S1), .At1(combinational_4_at1));
  Clock Clk (.out(Clk_out));
  D_Flip_Flop A0t (.D(combinational_1_at1), .clk(Clk_out), .Q(At1[0]), .reset(Reset));  // open: Qn, preset
  D_Flip_Flop A1t (.D(combinational_2_at1), .clk(Clk_out), .Q(At1[1]), .reset(Reset));  // open: Qn, preset
  D_Flip_Flop A2t (.D(combinational_3_at1), .clk(Clk_out), .Q(At1[2]), .reset(Reset));  // open: Qn, preset
  D_Flip_Flop A3t (.D(combinational_4_at1), .clk(Clk_out), .Q(At1[3]), .reset(Reset));  // open: Qn, preset
endmodule

module WithMux (
  input  S1,
  input  S0,
  input  [3:0] B,
  input  Reset,
  output [3:0] At1
);

  wire Clk_out, combinationalwithmux_1_at1, combinationalwithmux_2_at1, combinationalwithmux_3_at1,
       combinationalwithmux_4_at1;

  CombinationalWithMux combinationalwithmux_1 (
    .At(At1[0]), .B(B[0]), .S0(S0), .S1(S1), .At1(combinationalwithmux_1_at1));
  CombinationalWithMux combinationalwithmux_2 (
    .At(At1[1]), .B(B[1]), .S0(S0), .S1(S1), .At1(combinationalwithmux_2_at1));
  CombinationalWithMux combinationalwithmux_3 (
    .At(At1[2]), .B(B[2]), .S0(S0), .S1(S1), .At1(combinationalwithmux_3_at1));
  CombinationalWithMux combinationalwithmux_4 (
    .At(At1[3]), .B(B[3]), .S0(S0), .S1(S1), .At1(combinationalwithmux_4_at1));
  D_Flip_Flop A0t (.D(combinationalwithmux_1_at1), .clk(Clk_out), .Q(At1[0]), .reset(Reset));  // open: Qn, preset
  D_Flip_Flop A1t (.D(combinationalwithmux_2_at1), .clk(Clk_out), .Q(At1[1]), .reset(Reset));  // open: Qn, preset
  D_Flip_Flop A2t (.D(combinationalwithmux_3_at1), .clk(Clk_out), .Q(At1[2]), .reset(Reset));  // open: Qn, preset
  D_Flip_Flop A3t (.D(combinationalwithmux_4_at1), .clk(Clk_out), .Q(At1[3]), .reset(Reset));  // open: Qn, preset
  Clock Clk (.out(Clk_out));
endmodule
