// Logisim project LAB8_RBN_2306173113_AthazahraNabilaRubycirc.circ as structural Verilog: 2 circuits, main circuit Modified4BitCounter
module Modified4BitCounter (
  input  Reset,
  input  Clock,
  input  Load,
  input  Count,
  input  Inc2,
  input  Inc4,
  input  Inc8,
  input  [3:0] I,
  output [3:0] O,
  output CarryOut
);

  wire and_1_out, and_2_out, and_3_out, and_4_out, and_5_out, and_6_out, and_7_out, and_9_out, and_10_out,
       and_11_out, and_12_out, and_13_out, and_14_out, and_15_out, and_16_out, not_1_out, or_1_out, or_2_out,
       or_3_out, or_4_out, or_5_out, or_6_out, or_7_out, xor_1_out, xor_2_out, xor_3_out, xor_4_out;

  not not_1 (not_1_out, Load);
  and and_1 (and_1_out, Count, ~Inc2, ~Inc4, ~Inc8);  // AND_Gate
  and and_2 (and_2_out, Count, Inc2, ~Inc4, ~Inc8);  // AND_Gate
  and and_3 (and_3_out, Count, Inc4, ~Inc8);  // AND_Gate
  and and_4 (and_4_out, Count, Inc8);
  or or_1 (or_1_out, and_5_out, and_2_out);
  or or_2 (or_2_out, and_6_out, and_3_out);
  or or_3 (or_3_out, and_7_out, and_4_out);
  and and_5 (and_5_out, and_1_out, O[0]);
  and and_6 (and_6_out, or_1_out, O[1]);
  and and_7 (and_7_out, or_2_out, O[2]);
  and and_8 (CarryOut, or_3_out, O[3]);
  xor xor_1 (xor_1_out, and_1_out, O[0]);
  xor xor_2 (xor_2_out, or_1_out, O[1]);
  xor xor_3 (xor_3_out, or_2_out, O[2]);
  xor xor_4 (xor_4_out, or_3_out, O[3]);
  and and_9 (and_9_out, Load, I[0]);
  and and_10 (and_10_out, xor_1_out, not_1_out);
  and and_11 (and_11_out, Load, I[1]);
  and and_12 (and_12_out, xor_2_out, not_1_out);
  and and_13 (and_13_out, Load, I[2]);
  and and_14 (and_14_out, xor_3_out, not_1_out);
  and and_15 (and_15_out, Load, I[3]);
  and and_16 (and_16_out, xor_4_out, not_1_out);
  or or_4 (or_4_out, and_9_out, and_10_out);
  or or_5 (or_5_out, and_11_out, and_12_out);
  or or_6 (or_6_out, and_13_out, and_14_out);
  or or_7 (or_7_out, and_15_out, and_16_out);
  D_Flip_Flop D (.D(or_4_out), .clk(Clock), .Q(O[0]), .reset(Reset));  // open: Qn, preset
  D_Flip_Flop C (.D(or_5_out), .clk(Clock), .Q(O[1]), .reset(Reset));  // open: Qn, preset
  D_Flip_Flop B (.D(or_6_out), .clk(Clock), .Q(O[2]), .reset(Reset));  // open: Qn, preset
  D_Flip_Flop A (.D(or_7_out), .clk(Clock), .Q(O[3]), .reset(Reset));  // open: Qn, preset
  Hex_Digit_Display hex_digit_display_1 (.value(O));  // open: dp
endmodule

module Modified16BitCounter (
  input  Inc8,
  input  Inc4,
  input  Inc2,
  input  Count,
  input  Load,
  input  Reset,
  input  [3:0] Zx,
  input  [3:0] Yx,
  input  [3:0] Xx,
  input  [3:0] Wx,
  output [3:0] Dx,
  output [3:0] Cx,
  output [3:0] Bx,
  output [3:0] Ax
);

  wire Clk_out, modified4bitcounter_1_carryout, modified4bitcounter_2_carryout,
       modified4bitcounter_3_carryout;

  Clock Clk (.out(Clk_out));
  Modified4BitCounter modified4bitcounter_1 (
    .Reset(Reset), .Clock(Clk_out), .Load(Load), .Count(Count), .Inc2(Inc2), .Inc4(Inc4), .Inc8(Inc8),
    .I(Zx), .O(Dx), .CarryOut(modified4bitcounter_1_carryout));
  Modified4BitCounter modified4bitcounter_2 (
    .Reset(Reset), .Clock(Clk_out), .Load(Load), .Count(modified4bitcounter_1_carryout), .Inc2(1'b0),
    .Inc4(1'b0), .Inc8(1'b0), .I(Yx), .O(Cx), .CarryOut(modified4bitcounter_2_carryout));
  Modified4BitCounter modified4bitcounter_3 (
    .Reset(Reset), .Clock(Clk_out), .Load(Load), .Count(modified4bitcounter_2_carryout), .Inc2(1'b0),
    .Inc4(1'b0), .Inc8(1'b0), .I(Xx), .O(Bx), .CarryOut(modified4bitcounter_3_carryout));
  Modified4BitCounter modified4bitcounter_4 (
    .Reset(Reset), .Clock(Clk_out), .Load(Load), .Count(modified4bitcounter_3_carryout), .Inc2(1'b0),
    .Inc4(1'b0), .Inc8(1'b0), .I(Wx), .O(Ax));  // open: CarryOut
  Hex_Digit_Display hex_digit_display_1 (.value(Ax));  // open: dp
  Hex_Digit_Display hex_digit_display_2 (.value(Bx));  // open: dp
  Hex_Digit_Display hex_digit_display_3 (.value(Cx));  // open: dp
  Hex_Digit_Display hex_digit_display_4 (.value(Dx));  // open: dp
endmodule
